# Fritzing sketch ESP8266WeatherStation (saved by Fritzing 0.9.3b)
circuit board: 4.91903cm x 5.13502cm
breadboards: 2

parts:
  TFT1 = Color 320x240 TFT Display, ILI9341 Controller Chip
  U1 = NodeMCU V3.0
  DHT1 = DHT22 Humidity and Temperature Sensor
  R1 = Resistor [tolerance=±5% resistance=10k package=THT]
  BT1 = Bluetooth HC-06u [package=THT]

nets:
  VCC: TFT1.VCC, TFT1.Reset, TFT1.LED, U1.3V3, DHT1.VDD, R1.Pin_0, BT1.VCC
  GND: TFT1.GND, U1.GND, DHT1.GND, BT1.GND
  N1: TFT1.CS, U1.D8
  N2: TFT1.D/C, U1.D2
  N3: TFT1.SDI_(MOSI), U1.D7
  N4: TFT1.SCK, U1.D5
  N5: U1.D3, DHT1.DATA, R1.Pin_1
  N6: U1.D4, BT1.RXD
  N7: U1.D6, BT1.TXD

custom parts:
  Color 320x240 TFT Display, ILI9341 Controller Chip: 2.2" TFT Display with ILI9341 Controller
  NodeMCU V3.0: ESP8266 based NodeMCU
  Bluetooth HC-06u: Bluetooth HC-06 - face up, pins down 16.5mm x 37.5mm PCB
